// Logisim project comp.circ as structural Verilog: 1 circuit, main circuit main
module main (
);

  wire and_1_out, and_2_out, and_4_out, clock_1_out, decoder_1_out0, decoder_1_out1, decoder_1_out2,
       decoder_1_out3, decoder_1_out4, decoder_2_out0, decoder_2_out1, decoder_3_out0, decoder_3_out1,
       decoder_3_out2, not_1_out, or_1_out, pull_resistor_1_node;
  wire [2:0] counter_1_q;
  wire [3:0] multiplexer_3_out_2;
  wire [7:0] ACC_q, adder_1_out, adder_2_out, and_3_out, INST_q, multiplexer_1_out, multiplexer_2_out,
       multiplexer_3_out, multiplexer_4_out, not_2_out, or_2_out, ram_1_data, REGA_q, REGB_q, REGC_q,
       register_1_q, register_2_q, rom_1_data, xor_1_out;

  Counter #(.width(3), .max('h4)) counter_1 (.Q(counter_1_q), .clk(clock_1_out));  // open: load, D, count, carry, clr
  Clock clock_1 (.out(clock_1_out));
  Adder adder_1 (.a(8'h1), .b(register_2_q), .out(adder_1_out));  // open: cin, cout
  Register register_1 (.D(adder_1_out), .Q(register_1_q), .clk(decoder_1_out2));  // open: en, clr
  Multiplexer #(.width(8)) multiplexer_1 (
    .in0(register_1_q), .in1(ACC_q), .out(multiplexer_1_out), .sel(pull_resistor_1_node));  // open: en
  Decoder #(.select(3)) decoder_1 (
    .out0(decoder_1_out0), .out1(decoder_1_out1), .out2(decoder_1_out2), .out3(decoder_1_out3),
    .out4(decoder_1_out4), .sel(counter_1_q));  // open: out5, out6, out7, en
  Register register_2 (.D(multiplexer_1_out), .Q(register_2_q), .clk(decoder_1_out0));  // open: en, clr
  Register INST (
    .D(rom_1_data), .Q({INST_q[7:6], multiplexer_3_out[3:0], INST_q[1:0]}), .clk(decoder_1_out1));  // open: en, clr
  ROM rom_1 (.addr(register_2_q), .data(rom_1_data));  // open: sel
  Pull_Resistor pull_resistor_1 (.node(pull_resistor_1_node));
  // Probe on multiplexer_3_out
  // Probe on {multiplexer_3_out[3:0], multiplexer_3_out_2}
  Decoder #(.select(4), .tristate("true"), .disabled(0)) decoder_2 (
    .out0(decoder_2_out0), .out1(decoder_2_out1), .sel({INST_q[7:6], multiplexer_3_out[3:2]}));  // open: out2, out3, out4, out5, out6, out7, out8, out9, out10, out11, out12, out13, out14, out15, en
  Register REGA (.D(ACC_q), .Q(REGA_q), .clk(decoder_3_out0));  // open: en, clr
  Register REGB (.D(ACC_q), .Q(REGB_q), .clk(decoder_3_out1));  // open: en, clr
  Register REGC (.D(ACC_q), .Q(REGC_q), .clk(decoder_3_out2));  // open: en, clr
  Pull_Resistor pull_resistor_2 (.node(decoder_2_out0));
  Decoder #(.select(2), .tristate("true"), .disabled(0)) decoder_3 (
    .out0(decoder_3_out0), .out1(decoder_3_out1), .out2(decoder_3_out2), .out3(pull_resistor_1_node),
    .sel(INST_q[1:0]), .en(and_1_out));
  and and_1 (and_1_out, decoder_1_out4, not_1_out);
  // Probe on multiplexer_2_out
  Multiplexer #(.select(2), .width(8)) multiplexer_2 (
    .in0(REGA_q), .in1(REGB_q), .in2(REGC_q), .in3(register_2_q), .out(multiplexer_2_out),
    .sel(multiplexer_3_out[1:0]));  // open: en
  Multiplexer #(.select(2), .width(8)) multiplexer_3 (
    .in0(REGA_q), .in1(REGB_q), .in2(REGC_q), .in3(register_2_q),
    .out({multiplexer_3_out[7:4], multiplexer_3_out_2}), .sel(INST_q[1:0]));  // open: en
  not not_1 (not_1_out, decoder_2_out1);
  or or_1 (or_1_out, and_2_out, and_4_out);
  and and_2 (and_2_out, decoder_1_out2, decoder_2_out0);
  assign and_3_out = multiplexer_2_out & {multiplexer_3_out[7:4], multiplexer_3_out_2};  // AND_Gate and_3, 8 bits wide
  assign or_2_out = multiplexer_2_out | {multiplexer_3_out[7:4], multiplexer_3_out_2};  // OR_Gate or_2, 8 bits wide
  assign not_2_out = ~multiplexer_2_out;  // NOT_Gate not_2, 8 bits wide
  RAM #(.bus("separate")) ram_1 (
    .addr(multiplexer_2_out), .din(ACC_q), .data(ram_1_data), .str(decoder_2_out1), .clk(or_1_out),
    .ld(decoder_2_out0));  // open: sel, clr
  and and_4 (and_4_out, decoder_2_out1, decoder_1_out4);
  Adder adder_2 (
    .a(multiplexer_2_out), .b({multiplexer_3_out[7:4], multiplexer_3_out_2}), .out(adder_2_out));  // open: cin, cout
  assign xor_1_out = multiplexer_2_out ^ {multiplexer_3_out[7:4], multiplexer_3_out_2};  // XOR_Gate xor_1, 8 bits wide
  Pull_Resistor pull_resistor_3 (.node(decoder_2_out1));
  // Probe on ram_1_data
  Multiplexer #(.select(4), .width(8)) multiplexer_4 (
    .in0(ram_1_data), .in1({multiplexer_3_out[7:4], multiplexer_3_out_2}), .in2(and_3_out), .in3(or_2_out),
    .in4(adder_2_out), .in5(not_2_out), .in6(multiplexer_2_out), .in7(xor_1_out), .in8(multiplexer_3_out),
    .in9(multiplexer_3_out), .in10(multiplexer_3_out), .in11(multiplexer_3_out),
    .in12({multiplexer_3_out[3:0], multiplexer_3_out_2}),
    .in13({multiplexer_3_out[3:0], multiplexer_3_out_2}),
    .in14({multiplexer_3_out[3:0], multiplexer_3_out_2}),
    .in15({multiplexer_3_out[3:0], multiplexer_3_out_2}), .out(multiplexer_4_out),
    .sel({INST_q[7:6], multiplexer_3_out[3:2]}));  // open: en
  Register ACC (.D(multiplexer_4_out), .Q(ACC_q), .clk(decoder_1_out3));  // open: en, clr

  // Notes on the sheet:
  //   contents of rom_1 (hex, n*v repeats v):
  //   70 75 86 1 49 11 93
endmodule
