// Logisim project comp.circ as structural Verilog: 1 circuit, main circuit main
// PC
module main (
);

  wire and_1_out, and_2_out, and_3_out, clock_1_out, decoder_1_out0, decoder_1_out1, decoder_1_out2,
       decoder_1_out3, decoder_2_out0, decoder_2_out1, decoder_2_out15, decoder_3_out1, decoder_3_out2,
       decoder_3_out3, decoder_3_out4, decoder_3_out5, decoder_3_out6, decoder_3_out7, or_1_out;
  wire [1:0] counter_1_q;
  wire [7:0] ACC_q, ACC_T_1_q, adder_1_out, adder_2_out, and_4_out, B_q, bit_extender_1_out, C_q, D_q, E_q,
       F_q, INST_q, multiplexer_1_out, multiplexer_2_out, multiplexer_3_out, multiplier_1_out, not_1_out,
       or_2_out, PC_q, ram_1_data, rom_1_data, SP_q, xor_1_out;

  Clock clock_1 (.out(clock_1_out));
  Adder adder_1 (.a(PC_q), .b(8'h1), .out(adder_1_out));  // open: cin, cout
  Counter #(.width(2), .max('h3)) counter_1 (.Q(counter_1_q), .clk(clock_1_out));  // open: load, D, count, carry, clr
  Multiplexer #(.width(8)) multiplexer_1 (
    .in0(adder_1_out), .in1(ACC_T_1_q), .out(multiplexer_1_out), .sel(decoder_3_out7));  // open: en
  Register PC (.D(multiplexer_1_out), .Q(PC_q), .clk(decoder_1_out0));  // open: en, clr
  Decoder #(.select(2)) decoder_1 (
    .out0(decoder_1_out0), .out1(decoder_1_out1), .out2(decoder_1_out2), .out3(decoder_1_out3),
    .sel(counter_1_q));  // open: en
  Register INST (.D(rom_1_data), .Q(INST_q), .clk(decoder_1_out1));  // open: en, clr
  ROM rom_1 (.addr(PC_q), .data(rom_1_data));  // open: sel
  Decoder #(.select(5), .disabled(0)) decoder_2 (
    .out0(decoder_2_out0), .out1(decoder_2_out1), .out15(decoder_2_out15), .sel(INST_q[7:3]));  // open: out2, out3, out4, out5, out6, out7, out8, out9, out10, out11, out12, out13, out14, out16, out17, out18, out19, out20, out21, out22, out23, out24, out25, out26, out27, out28, out29, out30, out31, en
  Decoder #(.select(3), .disabled(0)) decoder_3 (
    .out1(decoder_3_out1), .out2(decoder_3_out2), .out3(decoder_3_out3), .out4(decoder_3_out4),
    .out5(decoder_3_out5), .out6(decoder_3_out6), .out7(decoder_3_out7), .sel(INST_q[2:0]), .en(and_1_out));  // open: out0
  and and_1 (and_1_out, decoder_2_out0, decoder_1_out3);
  Register ACC_T_1 (.D(ACC_q), .Q(ACC_T_1_q), .clk(decoder_1_out0));  // open: en, clr
  Register B (.D(ACC_q), .Q(B_q), .clk(decoder_3_out1));  // open: en, clr
  Register C (.D(ACC_q), .Q(C_q), .clk(decoder_3_out2));  // open: en, clr
  Register D (.D(ACC_q), .Q(D_q), .clk(decoder_3_out3));  // open: en, clr
  Register E (.D(ACC_q), .Q(E_q), .clk(decoder_3_out4));  // open: en, clr
  Register F (.D(ACC_q), .Q(F_q), .clk(decoder_3_out5));  // open: en, clr
  Register SP (.D(ACC_q), .Q(SP_q), .clk(decoder_3_out6));  // open: en, clr
  assign bit_extender_1_out = {{4{INST_q[3]}}, INST_q[3:0]};  // Bit_Extender bit_extender_1
  Multiplexer #(.select(3), .width(8)) multiplexer_2 (
    .in0(ACC_T_1_q), .in1(B_q), .in2(C_q), .in3(D_q), .in4(E_q), .in5(F_q), .in6(SP_q), .in7(PC_q),
    .out(multiplexer_2_out), .sel(INST_q[2:0]));  // open: en
  or or_1 (or_1_out, and_3_out, and_2_out);
  and and_2 (and_2_out, decoder_1_out2, decoder_2_out15);
  and and_3 (and_3_out, decoder_2_out1, decoder_1_out3);
  assign xor_1_out = multiplexer_2_out ^ ACC_T_1_q;  // XOR_Gate xor_1, 8 bits wide
  assign and_4_out = multiplexer_2_out & ACC_T_1_q;  // AND_Gate and_4, 8 bits wide
  assign or_2_out = multiplexer_2_out | ACC_T_1_q;  // OR_Gate or_2, 8 bits wide
  Adder adder_2 (.a(multiplexer_2_out), .b(ACC_T_1_q), .out(adder_2_out));  // open: cin, cout
  assign not_1_out = ~multiplexer_2_out;  // NOT_Gate not_1, 8 bits wide
  Multiplier multiplier_1 (.a(multiplexer_2_out), .b(ACC_T_1_q), .out(multiplier_1_out));  // open: cin, cout
  RAM #(.bus("separate")) ram_1 (
    .addr(multiplexer_2_out), .din(multiplexer_3_out), .data(ram_1_data), .str(decoder_2_out1),
    .clk(or_1_out), .ld(decoder_2_out15));  // open: sel, clr
  Multiplexer #(.select(5), .width(8)) multiplexer_3 (
    .in0(ACC_T_1_q), .in1(ACC_T_1_q), .in2(ACC_T_1_q), .in3(ACC_T_1_q), .in4(ACC_T_1_q), .in5(ACC_T_1_q),
    .in6(ACC_T_1_q), .in7(ACC_T_1_q), .in8(xor_1_out), .in9(and_4_out), .in10(or_2_out), .in11(adder_2_out),
    .in12(not_1_out), .in13(multiplier_1_out), .in14(multiplexer_2_out), .in15(ram_1_data),
    .in16(bit_extender_1_out), .in17(bit_extender_1_out), .in18({INST_q[7:4], ACC_T_1_q[3:0]}),
    .in19({INST_q[7:4], ACC_T_1_q[3:0]}), .in20(ACC_T_1_q), .in21(ACC_T_1_q), .in22(ACC_T_1_q),
    .in23(ACC_T_1_q), .in24(ACC_T_1_q), .in25(ACC_T_1_q), .in26(ACC_T_1_q), .in27(ACC_T_1_q),
    .in28(ACC_T_1_q), .in29(ACC_T_1_q), .in30(ACC_T_1_q), .in31(ACC_T_1_q), .out(multiplexer_3_out),
    .sel(INST_q[7:3]));  // open: en
  Register ACC (.D(multiplexer_3_out), .Q(ACC_q), .clk(decoder_1_out3));  // open: en, clr

  // Notes on the sheet:
  //   contents of rom_1 (hex, n*v repeats v):
  //   8f 6 85 1 8f 5e 6 84 5f e 83 91 7 81 5e 6 8f 9f 7 8f 5e 6 72 e 71 a5 81 2 83 93 7 71 2 8f 59 1 8f 5e
  //   6 84 5f e 83 91 7 81 5e 6 71 6a 2 72 1 7e 2 81 5e 6 7e 7
endmodule
